# Fritzing sketch pad (saved by Fritzing 0.9.3b)
breadboards: 1

parts:
  Pro_Micro1 = Pro Micro
  S1 = Pushbutton [package="[THT]"]
  S2 = Pushbutton [package="[THT]"]
  S3 = Pushbutton [package="[THT]"]
  S4 = Pushbutton [package="[THT]"]
  S5 = Pushbutton [package="[THT]"]
  S6 = Pushbutton [package="[THT]"]
  S7 = Pushbutton [package="[THT]"]
  S8 = Pushbutton [package="[THT]"]
  S9 = Pushbutton [package="[THT]"]
  S10 = Pushbutton [package="[THT]"]

nets:
  N1: Pro_Micro1.D7, S10.Pin_1, S10.Pin_2
  N2: Pro_Micro1.D8, S8.Pin_1, S8.Pin_2
  N3: Pro_Micro1.D9, S9.Pin_1, S9.Pin_2
  N4: S1.Pin_1, S1.Pin_2
  N5: S1.Pin_3, S1.Pin_4, S2.Pin_3, S2.Pin_4, S3.Pin_3, S3.Pin_4, S4.Pin_3, S4.Pin_4, S5.Pin_3, S5.Pin_4, S6.Pin_3, S6.Pin_4, S7.Pin_3, S7.Pin_4, S8.Pin_3, S8.Pin_4, S9.Pin_3, S9.Pin_4, S10.Pin_3, S10.Pin_4
  N6: S2.Pin_1, S2.Pin_2
  N7: S3.Pin_1, S3.Pin_2
  N8: S4.Pin_1, S4.Pin_2
  N9: S5.Pin_1, S5.Pin_2
  N10: S6.Pin_1, S6.Pin_2
  N11: S7.Pin_1, S7.Pin_2

notes:
  UP
  DOWN
  LEFT
  RIGHT
  Pads - Girls code it better 2017/18
  Code: https://goo.gl/UdFf25
  CLICK_LEFT
  JUMP

custom parts:
  Pro Micro: The SparkFun Pro Micro is a complete USB-based microcontoller development system, in a very small footprint, capable of implementing many types of projects. All programming can be done via the USB port.
